# Fritzing sketch receiver (saved by Fritzing 0.9.5d)
breadboards: 1

parts:
  Buzzer = Piezo Speaker
  Ebyte_transceiver = ossoyoo-lora-module
  VCC2 = Battery
  Arduino_Nano = Arduino Nano (Rev3.0)

nets:
  N1: Buzzer.pin1, VCC2.-, Arduino_Nano.GND
  N2: Buzzer.pin2, Arduino_Nano.D7
  N3: Ebyte_transceiver.M0, Arduino_Nano.D6
  N4: Ebyte_transceiver.M1, Arduino_Nano.D5
  N5: Ebyte_transceiver.RXD, Arduino_Nano.D3
  N6: Ebyte_transceiver.TXD, Arduino_Nano.D4
  N7: Ebyte_transceiver.AUX, Arduino_Nano.D2
  N8: VCC2.+, Arduino_Nano.VIN

notes:
  Receiver / Récepteur

custom parts:
  ossoyoo-lora-module: Osoyoo Long Distance wireless transceiver Uart LoRa Module.
  Battery: Your standard 2x 18650 battery pack (7,4 Volts)

// code stored in the sketch: sonnette_receiver.ino
#include <SoftwareSerial.h>
#include "EBYTE.h"
#include "pitches.h"

#define PIN_AX 2
#define PIN_TX 4
#define PIN_RX 3
#define PIN_M1 5
#define PIN_M0 6
#define BUZ    7

struct DATA {
  int State;
};

DATA Message;
unsigned long Last;

SoftwareSerial ESerial(PIN_RX, PIN_TX);
EBYTE Transceiver(&ESerial, PIN_M0, PIN_M1, PIN_AX);

int melody[] = {
  NOTE_C4, NOTE_G3, NOTE_G3, NOTE_A3, NOTE_G3, 0, NOTE_B3, NOTE_C4
};

int noteDurations[] = {
  4, 8, 8, 4, 4, 4, 4, 4
};

void setup() {
  ESerial.begin(9600);
  pinMode(LED_BUILTIN, OUTPUT);
  pinMode(BUZ, OUTPUT);
  Transceiver.init();
  digitalWrite(LED_BUILTIN, LOW);
  Transceiver.PrintParameters();
}

void loop() {
  if (Transceiver.available()) {
    Transceiver.GetStruct(&Message, sizeof(Message));
    if (Message.State == 1) {
      for (int i = 0; i <= 3; i++) {
        digitalWrite(LED_BUILTIN, HIGH);
        playMelody();
        delay(1000);
        digitalWrite(LED_BUILTIN, LOW);
      }
    } else {
      digitalWrite(LED_BUILTIN, LOW);
    }
    Last = millis();
  } else {
    digitalWrite(LED_BUILTIN, LOW);
    if ((millis() - Last) > 1000) {
      Last = millis();
    }
  }
}

void playMelody() {
  for (int thisNote = 0; thisNote < 8; thisNote++) {
    int noteDuration = 1000 / noteDurations[thisNote];
    tone(BUZ, melody[thisNote], noteDuration);
    int pauseBetweenNotes = noteDuration * 1.30;
    delay(pauseBetweenNotes);
    noTone(BUZ);
  }
}
